// Digital circuit 8-bit counter V2.dig as structural Verilog
module _8_bit_counter_V2 (
  input  clk,
  input  in_2,
  input  in_3,
  input  in_4
);

  wire _74590_1_pin1, _74590_1_pin2, _74590_1_pin3, _74590_1_pin4, _74590_1_pin5, _74590_1_pin6,
       _74590_1_pin7, _74590_1_pin9, _74590_1_pin15, GND, VCC;

  _74590 _74590_1 (
    .pin1(_74590_1_pin1), .pin2(_74590_1_pin2), .pin3(_74590_1_pin3), .pin4(_74590_1_pin4),
    .pin5(_74590_1_pin5), .pin6(_74590_1_pin6), .pin7(_74590_1_pin7), .pin8(GND), .pin9(_74590_1_pin9),
    .pin10(in_3), .pin11(clk), .pin12(in_4), .pin13(clk), .pin14(in_2), .pin15(_74590_1_pin15), .pin16(VCC));
  LED led_1 (.in(_74590_1_pin1));
  LED led_2 (.in(_74590_1_pin2));
  LED led_3 (.in(_74590_1_pin3));
  LED led_4 (.in(_74590_1_pin4));
  LED led_5 (.in(_74590_1_pin5));
  LED led_6 (.in(_74590_1_pin6));
  LED led_7 (.in(_74590_1_pin7));
  LED led_8 (.in(_74590_1_pin15));
  LED led_9 (.in(_74590_1_pin9));

  // Notes on the sheet:
  //   clk: Hz: 10
endmodule
