// Digital circuit 8-bit counter V3.dig as structural Verilog
module _8_bit_counter_V3 (
  input  PCE,
  input  PCI,
  input  RES,
  input  [7:0] BSI,
  input  CLK,
  input  nOE,
  output [7:0] BSO,
  output [7:0] OUT
);

  wire counterpreset_1_ovf;

  CounterPreset #(.Bits(8)) counterpreset_1 (
    .en(PCE), .C(CLK), .dir(1'b0), .in(BSI), .ld(PCI), .clr(RES), .out(OUT), .ovf(counterpreset_1_ovf));
  LED led_1 (.in(counterpreset_1_ovf));
  _74245 _74245_1 (
    .pin1(1'b1), .pin2(OUT[0]), .pin3(OUT[1]), .pin4(OUT[2]), .pin5(OUT[3]), .pin6(OUT[4]), .pin7(OUT[5]),
    .pin8(OUT[6]), .pin9(OUT[7]), .pin10(1'b0), .pin11(BSO[7]), .pin12(BSO[6]), .pin13(BSO[5]),
    .pin14(BSO[4]), .pin15(BSO[3]), .pin16(BSO[2]), .pin17(BSO[1]), .pin18(BSO[0]), .pin19(nOE), .pin20(1'b1));
endmodule
