// Digital circuit 8-bit counter V4.dig as structural Verilog
module _8_bit_counter_V4 (
  input  [7:0] BSI,
  input  nRES,
  input  CE,
  input  nWE,
  input  CLK,
  input  nOE,
  output [7:0] OUT,
  output [7:0] BSO
);

  wire _74161_1_pin15;

  _74161 _74161_1 (
    .pin1(nRES), .pin2(CLK), .pin3(BSI[0]), .pin4(BSI[1]), .pin5(BSI[2]), .pin6(BSI[3]), .pin7(CE),
    .pin8(1'b0), .pin9(nWE), .pin10(CE), .pin11(OUT[3]), .pin12(OUT[2]), .pin13(OUT[1]), .pin14(OUT[0]),
    .pin15(_74161_1_pin15), .pin16(1'b1));
  _74161 _74161_2 (
    .pin1(nRES), .pin2(CLK), .pin3(BSI[4]), .pin4(BSI[5]), .pin5(BSI[6]), .pin6(BSI[7]), .pin7(CE),
    .pin8(1'b0), .pin9(nWE), .pin10(_74161_1_pin15), .pin11(OUT[7]), .pin12(OUT[6]), .pin13(OUT[5]),
    .pin14(OUT[4]), .pin16(1'b1));  // open: pin15
  Buffer buffer_1 (.IN(OUT), .nOE(nOE), .OUT(BSO));
endmodule
