// Digital circuit 8-bit counter.dig as structural Verilog
module _8_bit_counter (
  input  clk,
  input  B0,
  input  B1,
  input  B2,
  input  B3,
  input  nCLR,
  input  B4,
  input  B5,
  input  B6,
  input  B7,
  input  CE,
  input  nJMP,
  output Q0,
  output Q1,
  output Q2,
  output Q3,
  output Q4,
  output Q5,
  output Q6,
  output Q7
);

  wire _7408_1_pin2, _7408_1_pin3, _7432_1_pin3, _74163_1_pin15;

  _74163 _74163_1 (
    .pin1(nCLR), .pin2(clk), .pin3(B0), .pin4(B1), .pin5(B2), .pin6(B3), .pin7(CE), .pin8(1'b0), .pin9(nJMP),
    .pin10(CE), .pin11(Q3), .pin12(Q2), .pin13(Q1), .pin14(Q0), .pin15(_74163_1_pin15), .pin16(1'b1));
  _7408 _7408_1 (
    .pin1(clk), .pin2(_7408_1_pin2), .pin3(_7408_1_pin3), .pin4(1'b0), .pin5(1'b0), .pin7(1'b0), .pin9(1'b1),
    .pin10(1'b1), .pin12(1'b1), .pin13(1'b1), .pin14(1'b1));  // open: pin6, pin8, pin11
  _7432 _7432_1 (
    .pin1(_74163_1_pin15), .pin2(_7408_1_pin3), .pin3(_7432_1_pin3), .pin4(1'b0), .pin5(1'b0), .pin7(1'b0),
    .pin9(1'b1), .pin10(1'b1), .pin12(1'b1), .pin13(1'b1), .pin14(1'b1));  // open: pin6, pin8, pin11
  _7404 _7404_1 (
    .pin1(nJMP), .pin2(_7408_1_pin2), .pin3(1'b0), .pin5(1'b0), .pin7(1'b0), .pin9(1'b1), .pin11(1'b1),
    .pin13(1'b1), .pin14(1'b1));  // open: pin4, pin6, pin8, pin10, pin12
  _74163 _74163_2 (
    .pin1(nCLR), .pin2(_7432_1_pin3), .pin3(B4), .pin4(B5), .pin5(B6), .pin6(B7), .pin7(CE), .pin8(1'b0),
    .pin9(nJMP), .pin10(CE), .pin11(Q7), .pin12(Q6), .pin13(Q5), .pin14(Q4), .pin16(1'b1));  // open: pin15
  // _74590 _74590_1: pin names not known; wires that end beside it: 1'b0

  // Notes on the sheet:
  //   clk: Hz: 5
endmodule
