// Digital circuit 8-bit register.dig as structural Verilog
module _8_bit_register (
  input  D0,
  input  D1,
  input  D2,
  input  D3,
  input  D4,
  input  D5,
  input  D6,
  input  D7,
  input  nOE,
  input  CLK,
  input  nIE,
  input  RES,
  output Q0,
  output Q1,
  output Q2,
  output Q3,
  output Q4,
  output Q5,
  output Q6,
  output Q7
);

  wire Q0_t, Q1_t, Q2_t, Q3_t, Q4_t, Q5_t, Q6_t, Q7_t;

  LED led_1 (.in(Q0_t));
  LED led_2 (.in(Q1_t));
  LED led_3 (.in(Q2_t));
  LED led_4 (.in(Q3_t));
  LED led_5 (.in(Q4_t));
  LED led_6 (.in(Q5_t));
  LED led_7 (.in(Q6_t));
  LED led_8 (.in(Q7_t));
  _74173 _74173_1 (
    .pin1(1'b0), .pin2(1'b0), .pin3(Q0_t), .pin4(Q1_t), .pin5(Q2_t), .pin6(Q3_t), .pin7(CLK), .pin8(1'b0),
    .pin9(nIE), .pin10(nIE), .pin11(D3), .pin12(D2), .pin13(D1), .pin14(D0), .pin15(RES), .pin16(1'b1));
  _74173 _74173_2 (
    .pin1(1'b0), .pin2(1'b0), .pin3(Q4_t), .pin4(Q5_t), .pin5(Q6_t), .pin6(Q7_t), .pin7(CLK), .pin8(1'b0),
    .pin9(nIE), .pin10(nIE), .pin11(D7), .pin12(D6), .pin13(D5), .pin14(D4), .pin15(RES), .pin16(1'b1));
  _74245 _74245_1 (
    .pin1(1'b1), .pin2(Q0_t), .pin3(Q1_t), .pin4(Q2_t), .pin5(Q3_t), .pin6(Q4_t), .pin7(Q5_t), .pin8(Q6_t),
    .pin9(Q7_t), .pin10(1'b0), .pin11(Q7), .pin12(Q6), .pin13(Q5), .pin14(Q4), .pin15(Q3), .pin16(Q2),
    .pin17(Q1), .pin18(Q0), .pin19(nOE), .pin20(1'b1));

  // Other names for the same wires on the sheet: IE = nIE; OE = nOE

  // Notes on the sheet:
  //   Stored data
endmodule
