// Digital circuit ALU.dig as structural Verilog
module ALU (
  input  A0,
  input  A1,
  input  A2,
  input  A3,
  input  A4,
  input  A5,
  input  A6,
  input  A7,
  input  B0,
  input  B1,
  input  B2,
  input  B3,
  input  B4,
  input  B5,
  input  B6,
  input  B7,
  input  SUB,
  input  OE,
  output Q0,
  output Q1,
  output Q2,
  output Q3,
  output Q4,
  output Q5,
  output Q6,
  output Q7,
  output CO
);

  wire Carry, S0, S1, S2, S3, S4, S5, S6, S7;

  _74283 _74283_1 (
    .pin1(S1), .pin2(B1), .pin3(A1), .pin4(S0), .pin5(A0), .pin6(B0), .pin7(SUB), .pin8(1'b0), .pin9(Carry),
    .pin10(S3), .pin11(B3), .pin12(A3), .pin13(S2), .pin14(A2), .pin15(B2), .pin16(1'b1));
  _74283 _74283_2 (
    .pin1(S5), .pin2(B5), .pin3(A5), .pin4(S4), .pin5(A4), .pin6(B4), .pin7(Carry), .pin8(1'b0), .pin9(CO),
    .pin10(S7), .pin11(B7), .pin12(A7), .pin13(S6), .pin14(A6), .pin15(B6), .pin16(1'b1));
  _74245 _74245_1 (
    .pin1(1'b1), .pin2(S0), .pin3(S1), .pin4(S2), .pin5(S3), .pin6(S4), .pin7(S5), .pin8(S6), .pin9(S7),
    .pin10(1'b0), .pin11(Q7), .pin12(Q6), .pin13(Q5), .pin14(Q4), .pin15(Q3), .pin16(Q2), .pin17(Q1),
    .pin18(Q0), .pin19(OE), .pin20(1'b1));
endmodule
