// Digital circuit Clock (just chips).dig as structural Verilog
module Clock__just_chips (
);

  // _7408 _7408_1: pin names not known
  // _7432 _7432_1: pin names not known
  // _7404 _7404_1: pin names not known
endmodule
