// Digital circuit LAMP-8 Block Schematic.dig as structural Verilog
module LAMP_8_Block_Schematic (
  input  in_1,
  input  in_2,
  input  in_3,
  input  in_4,
  input  in_5,
  input  in_6,
  input  in_7,
  input  in_8,
  input  in_9,
  input  in_10,
  input  in_11,
  input  in_12,
  input  RES,
  input  Automatic,
  input  CLK,
  input  clk_2
);

  wire _74138_1_pin9, _74138_1_pin10, _74138_1_pin11, _74138_1_pin12, _74138_1_pin13, _74138_1_pin14,
       _74138_1_pin15, _74161_1_pin1, A_q0, A_q1, A_q2, A_q3, A_q4, A_q5, A_q6, A_q7, ALO, alu_1_co,
       and_1_out, and_2_out, ARI, B_q0, B_q1, B_q2, B_q3, B_q4, B_q5, B_q6, B_q7, BRI, CF, CFI, CLK_t, EI,
       HLT, INSTRUCTION_q3, INSTRUCTION_q4, INSTRUCTION_q5, INSTRUCTION_q6, INSTRUCTION_q7, IRI, MEI,
       MEMORY_POINTER_p5, MEO, MICROCODE_alo, MICROCODE_ari, MICROCODE_bri, MICROCODE_cfi, MICROCODE_ei,
       MICROCODE_iri, MICROCODE_mei, MICROCODE_meo, MICROCODE_mpi, MICROCODE_ori, MICROCODE_pci,
       MICROCODE_pco, MICROCODE_rri, MICROCODE_rro, MICROCODE_uio, MPI, nCLK, not_2_out, not_3_out,
       not_4_out, not_5_out, or_1_out, ORI, PCE, PCI, PCO, RRI, RRO, SUB, sub_circuit_1_q0, sub_circuit_1_q1,
       sub_circuit_1_q2, sub_circuit_1_q3, sub_circuit_1_q4, sub_circuit_1_q5, sub_circuit_1_q6,
       sub_circuit_1_q7, UIO;
  wire [2:0] INST, MiC;
  wire [3:0] _8_bit_counter_v4_1_bso, _8_bit_counter_v4_1_bso_2, _8_bit_counter_v4_1_out,
       _8_bit_counter_v4_1_out_2, undriven, undriven_2;
  wire [6:0] undriven_3;

  Microcode MICROCODE (
    .INST(INST), .MiC(MiC), .CF(CF), .ARI(MICROCODE_ari), .BRI(MICROCODE_bri), .ORI(MICROCODE_ori),
    .UIO(MICROCODE_uio), .CFI(MICROCODE_cfi), .ALO(MICROCODE_alo), .SUB(SUB), .MEI(MICROCODE_mei),
    .MEO(MICROCODE_meo), .MPI(MICROCODE_mpi), .PCI(MICROCODE_pci), .PCO(MICROCODE_pco), .PCE(PCE),
    .IRI(MICROCODE_iri), .RRI(MICROCODE_rri), .RRO(MICROCODE_rro), .EI(MICROCODE_ei), .HLT(HLT));
  _7404 _7404_1 (
    .pin1(MICROCODE_mei), .pin2(MEI), .pin3(MICROCODE_meo), .pin4(MEO), .pin5(MICROCODE_mpi), .pin6(MPI),
    .pin7(1'b0), .pin8(RRI), .pin9(MICROCODE_rri), .pin10(IRI), .pin11(MICROCODE_iri), .pin12(PCO),
    .pin13(MICROCODE_pco), .pin14(1'b1));
  _7404 _7404_2 (
    .pin1(MICROCODE_rro), .pin2(RRO), .pin3(MICROCODE_ei), .pin4(EI), .pin5(MICROCODE_pci), .pin6(PCI),
    .pin7(1'b0), .pin9(1'b0), .pin11(1'b0), .pin13(1'b0), .pin14(1'b1));  // open: pin8, pin10, pin12
  not not_1 (nCLK, CLK_t);
  _7404 _7404_3 (
    .pin1(MICROCODE_ari), .pin2(ARI), .pin3(MICROCODE_bri), .pin4(BRI), .pin5(MICROCODE_uio), .pin6(UIO),
    .pin7(1'b0), .pin8(CFI), .pin9(MICROCODE_cfi), .pin10(ORI), .pin11(MICROCODE_ori), .pin12(ALO),
    .pin13(MICROCODE_alo), .pin14(1'b1));
  // _8_bit_register MEMORY_POINTER: pin names not known; wires that end beside it: 1'b0, CLK_t, MPI, RES, MEMORY_POINTER_p5
  _8_bit_counter_V4 _8_bit_counter_v4_1 (
    .BSI({_8_bit_counter_v4_1_bso_2, _8_bit_counter_v4_1_bso}), .nRES(not_2_out), .CE(PCE), .nWE(PCI),
    .CLK(CLK_t), .nOE(PCO), .OUT({_8_bit_counter_v4_1_out_2, _8_bit_counter_v4_1_out}),
    .BSO({_8_bit_counter_v4_1_bso_2, _8_bit_counter_v4_1_bso}));
  not not_2 (not_2_out, RES);
  Seven_Seg_Hex seven_seg_hex_1 (.d(_8_bit_counter_v4_1_out_2), .dp(1'b0));
  not not_3 (not_3_out, MEMORY_POINTER_p5);
  Seven_Seg_Hex seven_seg_hex_2 (.d(_8_bit_counter_v4_1_out), .dp(1'b0));
  RAMSinglePortSel #(.AddrBits(7), .Bits(8)) RAM (
    .A(undriven_3), .CS(MEMORY_POINTER_p5), .WE(~MEI), .OE(~MEO),
    .D({_8_bit_counter_v4_1_bso_2, _8_bit_counter_v4_1_bso}));
  EEPROM #(.AddrBits(7), .Bits(8)) ROM (
    .A(undriven_3), .CS(not_3_out), .WE(~1'b1), .OE(~MEO),
    .D({_8_bit_counter_v4_1_bso_2, _8_bit_counter_v4_1_bso}));
  _8_bit_register USER_INPUT (
    .D0(in_8), .D1(in_7), .D2(in_6), .D3(in_5), .D4(in_4), .D5(in_3), .D6(in_2), .D7(in_1), .nOE(UIO),
    .CLK(CLK_t), .nIE(1'b0), .RES(RES), .Q0(_8_bit_counter_v4_1_bso[0]), .Q1(_8_bit_counter_v4_1_bso[1]),
    .Q2(_8_bit_counter_v4_1_bso[2]), .Q3(_8_bit_counter_v4_1_bso[3]), .Q4(_8_bit_counter_v4_1_bso_2[0]),
    .Q5(_8_bit_counter_v4_1_bso_2[1]), .Q6(_8_bit_counter_v4_1_bso_2[2]), .Q7(_8_bit_counter_v4_1_bso_2[3]));
  // Probe on undriven_3
  Seven_Seg_Hex seven_seg_hex_3 (.d(_8_bit_counter_v4_1_bso_2), .dp(1'b0));
  _8_bit_register INSTRUCTION (
    .D0(_8_bit_counter_v4_1_bso[0]), .D1(_8_bit_counter_v4_1_bso[1]), .D2(_8_bit_counter_v4_1_bso[2]),
    .D3(_8_bit_counter_v4_1_bso[3]), .D4(_8_bit_counter_v4_1_bso_2[0]), .D5(_8_bit_counter_v4_1_bso_2[1]),
    .D6(_8_bit_counter_v4_1_bso_2[2]), .D7(_8_bit_counter_v4_1_bso_2[3]), .nOE(1'b0), .CLK(CLK_t), .nIE(IRI),
    .RES(RES), .Q0(INST[0]), .Q1(INST[1]), .Q2(INST[2]), .Q3(INSTRUCTION_q3), .Q4(INSTRUCTION_q4),
    .Q5(INSTRUCTION_q5), .Q6(INSTRUCTION_q6), .Q7(INSTRUCTION_q7));
  Seven_Seg_Hex seven_seg_hex_4 (.d(_8_bit_counter_v4_1_bso), .dp(1'b0));
  _8_bit_register A (
    .D0(_8_bit_counter_v4_1_bso[0]), .D1(_8_bit_counter_v4_1_bso[1]), .D2(_8_bit_counter_v4_1_bso[2]),
    .D3(_8_bit_counter_v4_1_bso[3]), .D4(_8_bit_counter_v4_1_bso_2[0]), .D5(_8_bit_counter_v4_1_bso_2[1]),
    .D6(_8_bit_counter_v4_1_bso_2[2]), .D7(_8_bit_counter_v4_1_bso_2[3]), .nOE(1'b0), .CLK(CLK_t), .nIE(ARI),
    .RES(RES), .Q0(A_q0), .Q1(A_q1), .Q2(A_q2), .Q3(A_q3), .Q4(A_q4), .Q5(A_q5), .Q6(A_q6), .Q7(A_q7));
  _8_bit_register B (
    .D0(_8_bit_counter_v4_1_bso[0]), .D1(_8_bit_counter_v4_1_bso[1]), .D2(_8_bit_counter_v4_1_bso[2]),
    .D3(_8_bit_counter_v4_1_bso[3]), .D4(_8_bit_counter_v4_1_bso_2[0]), .D5(_8_bit_counter_v4_1_bso_2[1]),
    .D6(_8_bit_counter_v4_1_bso_2[2]), .D7(_8_bit_counter_v4_1_bso_2[3]), .nOE(1'b0), .CLK(CLK_t), .nIE(BRI),
    .RES(RES), .Q0(B_q0), .Q1(B_q1), .Q2(B_q2), .Q3(B_q3), .Q4(B_q4), .Q5(B_q5), .Q6(B_q6), .Q7(B_q7));
  SUB_circuit sub_circuit_1 (
    .B0(B_q0), .B1(B_q1), .B2(B_q2), .B3(B_q3), .B4(B_q4), .B5(B_q5), .B6(B_q6), .B7(B_q7), .SUB(SUB),
    .Q0(sub_circuit_1_q0), .Q1(sub_circuit_1_q1), .Q2(sub_circuit_1_q2), .Q3(sub_circuit_1_q3),
    .Q4(sub_circuit_1_q4), .Q5(sub_circuit_1_q5), .Q6(sub_circuit_1_q6), .Q7(sub_circuit_1_q7));
  // _8_bit_register ARGUMENT: pin names not known; wires that end beside it: INSTRUCTION_q3, INSTRUCTION_q4, INSTRUCTION_q5, INSTRUCTION_q6, INSTRUCTION_q7, RRO, CLK_t, RRI, RES
  ALU alu_1 (
    .A0(A_q0), .A1(A_q1), .A2(A_q2), .A3(A_q3), .A4(A_q4), .A5(A_q5), .A6(A_q6), .A7(A_q7),
    .B0(sub_circuit_1_q0), .B1(sub_circuit_1_q1), .B2(sub_circuit_1_q2), .B3(sub_circuit_1_q3),
    .B4(sub_circuit_1_q4), .B5(sub_circuit_1_q5), .B6(sub_circuit_1_q6), .B7(sub_circuit_1_q7), .SUB(SUB),
    .OE(ALO), .Q0(_8_bit_counter_v4_1_bso[0]), .Q1(_8_bit_counter_v4_1_bso[1]),
    .Q2(_8_bit_counter_v4_1_bso[2]), .Q3(_8_bit_counter_v4_1_bso[3]), .Q4(_8_bit_counter_v4_1_bso_2[0]),
    .Q5(_8_bit_counter_v4_1_bso_2[1]), .Q6(_8_bit_counter_v4_1_bso_2[2]), .Q7(_8_bit_counter_v4_1_bso_2[3]),
    .CO(alu_1_co));
  and and_1 (and_1_out, CLK, not_4_out);
  not not_4 (not_4_out, Automatic);
  and and_2 (and_2_out, clk_2, Automatic);
  LED led_1 (.in(CF));
  // _8_bit_register OUTPUT: pin names not known; wires that end beside it: 1'b0, CLK_t, ORI, RES
  or or_1 (or_1_out, and_1_out, and_2_out);
  _74173 _74173_1 (
    .pin1(1'b0), .pin2(1'b0), .pin3(CF), .pin7(CLK_t), .pin8(1'b0), .pin9(CFI), .pin10(CFI), .pin11(1'b0),
    .pin12(1'b0), .pin13(1'b0), .pin14(alu_1_co), .pin15(RES), .pin16(1'b1));  // open: pin4, pin5, pin6
  and and_3 (CLK_t, or_1_out, not_5_out);
  not not_5 (not_5_out, HLT);
  LED led_2 (.in(HLT));
  Seven_Seg_Hex seven_seg_hex_5 (.d(undriven), .dp(1'b0));
  Seven_Seg_Hex seven_seg_hex_6 (.d(undriven_2), .dp(1'b0));
  _74161 _74161_1 (
    .pin1(_74161_1_pin1), .pin2(nCLK), .pin3(in_9), .pin4(in_10), .pin5(in_11), .pin6(in_12), .pin7(1'b1),
    .pin8(1'b0), .pin9(1'b1), .pin10(1'b1), .pin12(MiC[2]), .pin13(MiC[1]), .pin14(MiC[0]), .pin16(1'b1));  // open: pin11, pin15
  _74138 _74138_1 (
    .pin1(MiC[0]), .pin2(MiC[1]), .pin3(MiC[2]), .pin4(1'b0), .pin5(1'b0), .pin6(1'b1), .pin7(_74161_1_pin1),
    .pin8(1'b0), .pin9(_74138_1_pin9), .pin10(_74138_1_pin10), .pin11(_74138_1_pin11),
    .pin12(_74138_1_pin12), .pin13(_74138_1_pin13), .pin14(_74138_1_pin14), .pin15(_74138_1_pin15),
    .pin16(1'b1));
  LED led_3 (.in(_74138_1_pin15));
  LED led_4 (.in(_74138_1_pin14));
  LED led_5 (.in(_74138_1_pin13));
  LED led_6 (.in(_74138_1_pin12));
  LED led_7 (.in(_74138_1_pin11));
  LED led_8 (.in(_74138_1_pin10));
  LED led_9 (.in(_74138_1_pin9));
  LED led_10 (.in(_74161_1_pin1));

  // Notes on the sheet:
  //   clk_2: Hz: 5
  //   Microcode
  //   Output Logic
  //   Memory Pointer + Memory
  //   User Input Reg
  //   Program Counter
  //   contents of ROM (hex, n*v repeats v):
  //   4,80,4,81,4,83,0,80,1,81,2,82,5,82,7
  //   Instruction Reg + Argument Reg
  //   Data Bus
  //   A Reg
  //   B Reg
  //   SUB Circuit
  //   ALU
  //   Output Reg
  //   Clock
  //   Carry Flag Reg
  //   Micro-instruction Counter
  //   LAMP-8 Minicomputer
  //   > 8-bit data width
  //    > 8-bit address space
  //    > 8 instructions
  //    > "24-bit" control word
  //    > Basic I/O capabilities
  //    > Turing-complete :)
endmodule
