// Digital circuit RAM.dig as structural Verilog
module RAM (
  input  VCC,
  input  GND,
  input  A0,
  input  A1,
  input  A2,
  input  A3,
  input  A4,
  input  A5,
  input  A6,
  input  A7,
  input  A8,
  input  A9,
  input  A10,
  input  A11,
  input  A12,
  input  A13,
  input  A14,
  input  nCE,
  input  nWE,
  input  nOE,
  input  I_O_0,
  input  I_O_1,
  input  I_O_2,
  input  I_O_3,
  input  I_O_4,
  input  I_O_5,
  input  I_O_6,
  input  I_O_7,
  output I_O_0_2,
  output I_O_1_2,
  output I_O_2_2,
  output I_O_3_2,
  output I_O_4_2,
  output I_O_5_2,
  output I_O_6_2,
  output I_O_7_2
);

  PowerSupply powersupply_1 (.VDD(VCC), .GND(GND));
  RAMSinglePortSel #(.AddrBits(15), .Bits(8)) ramsingleportsel_1 (
    .A({A14, A13, A12, A11, A10, A9, A8, A7, A6, A5, A4, A3, A2, A1, A0}), .CS(~nCE), .WE(~nWE), .OE(~nOE),
    .D({I_O_7, I_O_6, I_O_5, I_O_4, I_O_3, I_O_2, I_O_1, I_O_0}));

  assign I_O_0_2 = I_O_0;
  assign I_O_1_2 = I_O_1;
  assign I_O_2_2 = I_O_2;
  assign I_O_3_2 = I_O_3;
  assign I_O_4_2 = I_O_4;
  assign I_O_5_2 = I_O_5;
  assign I_O_6_2 = I_O_6;
  assign I_O_7_2 = I_O_7;

  // Notes on the sheet:
  //   VCC: default 1
  //   CY7C199
endmodule
