// Digital circuit SUB circuit.dig as structural Verilog
module SUB_circuit (
  input  B0,
  input  B1,
  input  B2,
  input  B3,
  input  B4,
  input  B5,
  input  B6,
  input  B7,
  input  SUB,
  output Q0,
  output Q1,
  output Q2,
  output Q3,
  output Q4,
  output Q5,
  output Q6,
  output Q7
);

  _7486 _7486_1 (
    .pin1(B0), .pin2(SUB), .pin3(Q0), .pin4(B1), .pin5(SUB), .pin6(Q1), .pin7(1'b0), .pin8(Q2), .pin9(B2),
    .pin10(SUB), .pin11(Q3), .pin12(B3), .pin13(SUB), .pin14(1'b1));
  _7486 _7486_2 (
    .pin1(B4), .pin2(SUB), .pin3(Q4), .pin4(B5), .pin5(SUB), .pin6(Q5), .pin7(1'b0), .pin8(Q6), .pin9(B6),
    .pin10(SUB), .pin11(Q7), .pin12(B7), .pin13(SUB), .pin14(1'b1));
endmodule
