// Digital circuit microcode test.dig as structural Verilog
module microcode_test (
  input  [2:0] INST,
  input  [2:0] MiC,
  input  CF,
  output ARI,
  output BRI,
  output ORI,
  output UIO,
  output CFI,
  output ALO,
  output SUB,
  output MEI,
  output MEO,
  output MPI,
  output PCI,
  output PCO,
  output PCE,
  output IRI,
  output RRI,
  output RRO,
  output EI,
  output HLT
);

  wire [7:2] _0_d;

  ROM #(.AddrBits(7), .Bits(8)) _2 (.A({MiC, INST, CF}), .sel(1'b1), .D({MEI, SUB, ALO, CFI, UIO, ORI, BRI, ARI}));
  ROM #(.AddrBits(7), .Bits(8)) _1 (.A({MiC, INST, CF}), .sel(1'b1), .D({RRO, RRI, IRI, PCE, PCO, PCI, MPI, MEO}));
  ROM #(.AddrBits(7), .Bits(8)) _0 (.A({MiC, INST, CF}), .sel(1'b1), .D({_0_d, HLT, EI}));

  // Notes on the sheet:
  //   contents of _2 (hex, n*v repeats v):
  //   80*0,1,1,2,2,b0,b0,f0,f0,88,88,4,4
  //   contents of _1 (hex, n*v repeats v):
  //   16*a,16*31,16*a,16*51,12*82,0,82,0,0,4*1,6*0,1,1,0,5
  //   contents of _0 (hex, n*v repeats v):
  //   76*0,1,0,2,2,14*0,14*1,0,1
endmodule
